// Logisim project uart.circ as structural Verilog: 1 circuit, main circuit main
module main (
);

  wire and_1_out, and_2_out, and_3_out, and_4_out, and_5_out, clock_1_out, clock_2_out, not_2_out, not_3_out,
       or_1_out, pull_resistor_1_node, pull_resistor_2_node, pull_resistor_4_node, pull_resistor_5_node, TX,
       TX_ENB_out, U1_74LS194_p2, U2_74LS194_p7, U3_74LS194_p7, U3_74LS194_p13, U10_74LS279_q, U13_74LS279_q;
  wire [3:0] U5_74LS194_p4, U5_74LS194_p10, U6_74LS163_q;
  wire [7:0] ledbar_1_p1, U9_74LS273_q;

  Button TX_ENB (.out(TX_ENB_out));
  Clock clock_1 (.out(clock_1_out));
  // LedBar #(.inputtype("row")) ledbar_1: pin names not known; wires that end beside it: ledbar_1_p1
  DipSwitch TX_DATA (
    .sw1(ledbar_1_p1[7]), .sw2(ledbar_1_p1[6]), .sw3(ledbar_1_p1[5]), .sw4(ledbar_1_p1[4]),
    .sw5(ledbar_1_p1[3]), .sw6(ledbar_1_p1[2]), .sw7(ledbar_1_p1[1]), .sw8(ledbar_1_p1[0]));
  Pull_Resistor pull_resistor_1 (.node(pull_resistor_1_node));
  Pull_Resistor #(.pull(1)) pull_resistor_2 (.node(pull_resistor_2_node));
  // Shift_Register #(.length(4)) U1_74LS194: pin names not known; wires that end beside it: TX_ENB_out, U1_74LS194_p2, clock_1_out, pull_resistor_1_node, pull_resistor_1_node
  not not_1 (U1_74LS194_p2, TX_ENB_out);
  // Shift_Register #(.length(4)) U2_74LS194: pin names not known; wires that end beside it: pull_resistor_1_node, pull_resistor_1_node, ledbar_1_p1[7], TX_ENB_out, U1_74LS194_p2, clock_1_out, U2_74LS194_p7, ledbar_1_p1[6], U2_74LS194_p7
  // Shift_Register #(.length(4)) U3_74LS194: pin names not known; wires that end beside it: ledbar_1_p1[5], ledbar_1_p1[4], ledbar_1_p1[3], TX_ENB_out, U1_74LS194_p2, clock_1_out, U3_74LS194_p7, ledbar_1_p1[2], ledbar_1_p1[1], ledbar_1_p1[0], pull_resistor_2_node, U3_74LS194_p7, U3_74LS194_p13
  Pull_Resistor #(.pull(1)) pull_resistor_3 (.node(TX));
  Transistor #(.\type ("n")) transistor_1 (.in(1'b0), .out(TX), .gate(U3_74LS194_p13));
  Clock clock_2 (.out(clock_2_out));
  Pull_Resistor #(.pull(1)) pull_resistor_4 (.node(pull_resistor_4_node));
  Counter #(.max('hf), .width(4)) U6_74LS163 (
    .clr(and_4_out), .load(and_4_out), .up(pull_resistor_4_node), .count(U10_74LS279_q), .clk(clock_2_out),
    .Q(U6_74LS163_q));  // open: D, carry
  and and_1 (and_1_out, and_4_out, TX);
  not not_2 (not_2_out, TX);
  and and_2 (and_2_out, not_2_out, and_3_out);
  or or_1 (or_1_out, not_2_out, and_1_out);
  S_R_Flip_Flop #(.trigger("high")) U10_74LS279 (
    .S(and_2_out), .R(and_4_out), .clk(pull_resistor_4_node), .Q(U10_74LS279_q));  // open: reset, Qn, preset
  and and_3 (and_3_out, ~U6_74LS163_q[0], ~U6_74LS163_q[1], ~U6_74LS163_q[2], ~U6_74LS163_q[3]);  // AND_Gate
  and and_4 (and_4_out, U6_74LS163_q[0], ~U6_74LS163_q[1], ~U6_74LS163_q[2], U6_74LS163_q[3]);  // AND_Gate
  and and_5 (and_5_out, U10_74LS279_q, not_3_out);
  not not_3 (not_3_out, U10_74LS279_q);
  // Shift_Register #(.length(4)) U4_74LS194: pin names not known; wires that end beside it: and_5_out, U10_74LS279_q, clock_2_out, or_1_out, U5_74LS194_p4[3]
  // Shift_Register #(.length(4)) U5_74LS194: pin names not known; wires that end beside it: and_5_out, U10_74LS279_q, clock_2_out, U5_74LS194_p4[0], U5_74LS194_p4[2], U5_74LS194_p4[1], U5_74LS194_p10[3], U5_74LS194_p10[2], U5_74LS194_p10[1], U5_74LS194_p10[0]
  Register U9_74LS273 (
    .D({U5_74LS194_p4, U5_74LS194_p10}), .en(U10_74LS279_q), .clk(and_4_out), .Q(U9_74LS273_q),
    .clr(and_5_out));
  S_R_Flip_Flop #(.trigger("high")) U13_74LS279 (
    .S(and_4_out), .R(and_5_out), .clk(pull_resistor_5_node), .Q(U13_74LS279_q));  // open: reset, Qn, preset
  Pull_Resistor #(.pull(1)) pull_resistor_5 (.node(pull_resistor_5_node));
  // LedBar #(.inputtype("row")) RX_DATA: pin names not known; wires that end beside it: U9_74LS273_q
  LED DATA_RDY (.in(U13_74LS279_q));

  // Notes on the sheet:
  //   TX CIRCUIT
  //   Turned out to be quite simple, thankfully
  //   Q1_2N7000
  //   U11_74LS08
  //   U12_74LS32
  //   Q2_2N7000
  //   U7_74LS21
  //   U8_74LS14
  //   RX CIRCUIT
  //   Yes, it's messy...
endmodule
